// Logisim project LC-3.circ as structural Verilog: 15 circuits, main circuit main
module main (
  input  Reset,
  output out_2,
  output out_3,
  output out_4,
  output out_5,
  output out_6,
  output out_7,
  output out_8,
  output [15:0] out_9,
  output [15:0] out_10,
  output [15:0] out_11,
  output [15:0] out_12,
  output [15:0] out_13,
  output [15:0] out_14,
  output [15:0] out_15,
  output [15:0] out_16,
  output [15:0] out_17,
  output halt,
  output [15:0] out_19,
  output [15:0] out_20,
  output [15:0] out_21,
  output [15:0] out_22
);

  wire decodeir_1_writereg, getcst_1_usecst, or16_1_out_2, or16_2_out_2, ramctrl_1_memload,
       ramctrl_1_memstore;
  wire [2:0] nzp_1_nzp_2;
  wire [15:0] getcst_1_cst, RegIN, registres_1_out_sr1, registres_1_out_sr2;

  BiClock biclock_1 (.reset(Reset), .signal0(out_2), .signal1(out_3));
  RegPC regpc_1 (
    .H(out_3), .PC(out_9), .Reset(Reset), .IR(out_10), .R(registres_1_out_sr1), .TestNZP(out_5), .Jump(out_4));
  // Probe on out_9
  // Probe on out_11
  GetAddr getaddr_1 (.PC(out_9), .R(registres_1_out_sr1), .IR(out_10), .Addr(out_11), .Fetch(out_2));
  // Probe on out_12
  LED led_1 (.in(out_6));
  RamCtrl ramctrl_1 (
    .Store(out_7), .Fetch(out_2), .Exec(out_3), .Load(out_6), .MemStore(ramctrl_1_memstore),
    .MemLoad(ramctrl_1_memload));
  LED led_2 (.in(out_7));
  // Probe on out_13
  RAM #(.addrWidth(16), .dataWidth(16), .bus("separate")) ram_1 (
    .addr(out_11), .din(out_12), .data(out_13), .str(ramctrl_1_memstore), .clk(ramctrl_1_memstore),
    .ld(ramctrl_1_memload));  // open: sel, clr
  Register #(.width(16), .trigger("falling")) RegIR (.D(out_13), .Q(out_10), .clk(out_2));  // open: en, clr
  DecodeIR decodeir_1 (
    .IR(out_10), .Jump(out_4), .WriteReg(decodeir_1_writereg), .Load(out_6), .Store(out_7));  // open: Arith
  // Probe on out_10[11:9]
  // Probe on out_10[8:6]
  // Probe on out_10[2:0]
  // Probe on getcst_1_cst
  GetCst getcst_1 (.IR(out_10), .Cst(getcst_1_cst), .UseCst(getcst_1_usecst));
  // Probe on out_10[15:14]
  and and_1 (out_8, decodeir_1_writereg, out_3);
  Registres registres_1 (
    .SR1(out_10[8:6]), .IN(RegIN), .SR2(out_10[2:0]), .WriteReg(out_8), .DR_SR(out_10[11:9]),
    .OUT_SR1(registres_1_out_sr1), .OUT_SR2(registres_1_out_sr2), .R0(out_14), .R1(out_15), .R2(out_16),
    .R3(out_17), .R4(out_19), .R5(out_20), .R6(out_21), .R7(out_22));  // open: OUT_SR
  // Probe on registres_1_out_sr1
  ALU alu_1 (
    .UseCst(getcst_1_usecst), .e2(out_10[15:14]), .Input1(registres_1_out_sr1), .Input2(registres_1_out_sr2),
    .Cst(getcst_1_cst), .Output(RegIN));
  // Probe on registres_1_out_sr2
  // Probe on RegIN
  NZP nzp_1 (.RES(RegIN), .NZP_2(nzp_1_nzp_2), .IR(out_10), .TestNZP(out_5), .WriteReg(out_8));  // open: NZP
  Or16 or16_1 (.in_1(out_10), .out_2(or16_1_out_2));
  Or16 or16_2 (.in_1(out_9), .out_2(or16_2_out_2));
  // Probe on out_14
  // Probe on out_15
  // Probe on out_16
  // Probe on out_17
  // Probe on out_19
  // Probe on out_20
  // Probe on out_21
  // Probe on out_22
  // Probe on nzp_1_nzp_2
  and and_2 (halt, ~or16_1_out_2, or16_2_out_2);  // AND_Gate

  // Other names for the same wires on the sheet: Addr[15:0] = out_11; Condition = out_5; Exec = out_3; Fetch = out_2;
  //   IR[15:0] = out_10; JumpInstr = out_4; Load = out_6; MemIN[15:0] = out_12; MemOUT[15:0] = out_13;
  //   PC[15:0] = out_9; R0[15:0] = out_14; R1[15:0] = out_15; R2[15:0] = out_16; R3[15:0] = out_17; R4[15:0] = out_19;
  //   R5[15:0] = out_20; R6[15:0] = out_21; R7[15:0] = out_22; Store = out_7; WriteReg = out_8

  // Notes on the sheet:
  //   R
  //   IR
  //   R
  //   IR
  //   RAM
  //   Traces (NE PAS MODIFIER)______________________________________________________________________________________________________
  //   GetRegs
  //   GetOp
  //   Arret des traces au 1er NOP
endmodule

module ALU (
  input  [15:0] Input1,
  input  [15:0] Input2,
  input  [15:0] Cst,
  input  UseCst,
  input  [1:0] e2,
  output [15:0] Output
);

  wire adder_1_cout, undriven;
  wire [15:0] adder_1_out, and_1_out, multiplexer_1_out, not_1_out;

  Multiplexer #(.width(16), .enable("false")) multiplexer_1 (
    .in0(Input2), .in1(Cst), .out(multiplexer_1_out), .sel(UseCst));
  Adder #(.width(16)) adder_1 (
    .a(multiplexer_1_out), .b(Input1), .out(adder_1_out), .cin(undriven), .cout(adder_1_cout));
  assign and_1_out = Input1 & multiplexer_1_out;  // AND_Gate and_1, 16 bits wide
  Multiplexer #(.select(2), .width(16), .enable("false")) multiplexer_2 (
    .in0(adder_1_out), .in1(and_1_out), .in2(not_1_out), .out(Output), .sel(e2));  // open: in3
  assign not_1_out = ~Input1;  // NOT_Gate not_1, 16 bits wide
endmodule

module BiClock (
  input  reset,
  output signal0,
  output signal1
);

  wire and_1_out, horloge_out, not_1_out, register_1_q;

  Clock horloge (.out(horloge_out));
  not not_1 (not_1_out, register_1_q);
  Register #(.width(1), .trigger("falling")) register_1 (
    .D(not_1_out), .Q(register_1_q), .clk(horloge_out), .clr(reset));  // open: en
  and and_1 (and_1_out, horloge_out, ~reset);  // AND_Gate
  and and_2 (signal0, ~register_1_q, and_1_out);  // AND_Gate
  and and_3 (signal1, register_1_q, and_1_out);

  // Notes on the sheet:
  //   Ce module divise une horloge en deux sous-horloges alternées
  //   Chronogrammes :
  //   horloge: 0101010101 signal0: 0100010001 signal1: 000100010
  //   registre 1-bit
  //   Enable
  //   select : 0 / 1
endmodule

module DecodeIR (
  input  [15:0] IR,
  output Arith,
  output Jump,
  output Load,
  output Store,
  output WriteReg
);

  wire not_1_out, not_2_out, not_3_out, not_4_out, not_5_out, not_6_out;

  // NOT_Gate not_1 has open pins: in=open, out=not_1_out
  // NOT_Gate not_2 has open pins: in=open, out=not_2_out
  // AND_Gate and_1 has open pins: in0=not_1_out, in1=not_2_out, out=open
  nor nor_1 (Arith, IR[13], not_3_out);
  not not_3 (not_3_out, IR[12]);
  nor nor_2 (Jump, IR[13], IR[12]);
  not not_4 (not_4_out, IR[13]);
  nor nor_3 (Load, not_4_out, IR[12]);
  not not_5 (not_5_out, IR[13]);
  nor nor_4 (Store, not_5_out, not_6_out);
  not not_6 (not_6_out, IR[12]);
  or or_1 (WriteReg, Arith, Load, Store);

  // Notes on the sheet:
  //   version de base (JMP):
  //   sauf que AND, c'est NAND+NOT
  //   NOT(NOT(a.b)) = NOT(NOT(a)+NOT(b))
  //   soit NOR(NOT(a),NOT(b) )
  //   On n'a pas gagné sur les portes NOT
  //   mais un NOR prend moins de
  //   transistors qu'un AND
  //   On prend les 13e et 12e bits de IR, 
  //   Cela nous donne l'op-code
  //   Direction ALU
  //   Si op-code finit par 00 :
  //   Direction Jump
  //   SI op-code finit par 01 :
  //   Si op-code finit par 10 :
  //   Direction Load
  //   Si op-code finit par 11 : 
  //   Direction Store
  //   Est-ce que c'est vrai ?
  //   Instruction modifiant les registres
  //   (toujours oui pour l'instant)
endmodule

module GetAddr (
  input  [15:0] PC,
  input  Fetch,
  input  [15:0] IR,
  input  [15:0] R,
  output [15:0] Addr
);

  wire checkbr_1_yes_no, checkjmp_1_yes_no, or_1_out;
  wire [15:0] adder_1_out, bit_extender_1_out, multiplexer_1_out, multiplexer_2_out;

  // Probe on IR[15:12]
  CheckBR checkbr_1 (.op_code(IR[15:12]), .yes_no(checkbr_1_yes_no));
  CheckJMP checkjmp_1 (.op_code(IR[15:12]), .yes_no(checkjmp_1_yes_no));
  assign bit_extender_1_out = {{7{IR[8]}}, IR[8:0]};  // Bit_Extender bit_extender_1
  or or_1 (or_1_out, checkbr_1_yes_no, checkjmp_1_yes_no);
  Adder #(.width(16)) adder_1 (.a(PC), .b(bit_extender_1_out), .out(adder_1_out));  // open: cin, cout
  // Probe on adder_1_out
  // Probe on multiplexer_1_out
  Multiplexer #(.width(16)) multiplexer_1 (
    .in0(PC), .in1(multiplexer_2_out), .out(multiplexer_1_out), .sel(or_1_out));  // open: en
  Multiplexer #(.width(16)) multiplexer_2 (
    .in0(adder_1_out), .in1(R), .out(multiplexer_2_out), .sel(IR[15]));  // open: en
  Multiplexer #(.width(16)) multiplexer_3 (.in0(PC), .in1(multiplexer_1_out), .out(Addr), .sel(Fetch));  // open: en
  // Probe on multiplexer_2_out

  // Notes on the sheet:
  //   Si l'instruction est différente de BR ou JMP
  //   on ne devrait pas modifier l'adresse
  //   le 1er bit de l'op-code est 
  //   0 pour BR
  //   1 pour JMP
  //   Adresse Memoire
  //   si l'instruction est BR, la prochaine adresse
  //   sera PC+offset9
  //   sinon ce sera peut-être un JMP
  //   (toujours PC pour l'instant)
endmodule

module GetCst (
  input  [15:0] IR,
  output [15:0] Cst,
  output UseCst
);

  assign Cst = {{11{IR[4]}}, IR[4:0]};  // Bit_Extender bit_extender_1

  assign UseCst = IR[5];
endmodule

// 16
module NZP (
  input  [2:0] NZP,
  input  [15:0] RES,
  input  [15:0] IR,
  input  WriteReg,
  output [2:0] NZP_2,
  output TestNZP
);

  wire [2:0] not_1_out;
  wire [15:0] or_1_out;

  and and_1 (not_1_out[2], 1'b1, RES[15]);
  assign or_1_out = RES | {16{1'b0}};  // OR_Gate or_1, 16 bits wide
  not not_1 (not_1_out[0], or_1_out[0]);
  Multiplexer #(.width(3)) multiplexer_1 (
    .in0({not_1_out[2], or_1_out[0], not_1_out[0]}), .in1(NZP), .out(NZP_2), .sel(WriteReg));  // open: en

  assign TestNZP = 1'b0;

  // Notes on the sheet:
  //   Entrées non utilisées pour l'instant
  //   (Resultat du calcul courant)
  //   (Instruction courante)
  //   (Instruction mettant à jour NZP)
  //   Ici, RES est négatif
  //   Ici, RES est 0
  //   Ici, RES est positif
  //   Test de saut
  //   Valeur actuel du registre d'état NZP
endmodule

// Off6
module Offset6 (
  input  [15:0] IR,
  output [15:0] Off6
);

  assign Off6 = {{10{IR[5]}}, IR[5:0]};  // Bit_Extender bit_extender_1
endmodule

// Off9
module Offset9 (
  input  [15:0] IR,
  output [15:0] Off9
);

  assign Off9 = {{7{IR[8]}}, IR[8:0]};  // Bit_Extender bit_extender_1
endmodule

module Or16 (
  input  [15:0] in_1,
  output out_2
);

  wire [3:0] or_1_out;

  assign or_1_out = in_1[3:0] | in_1[7:4] | in_1[11:8] | in_1[15:12];  // OR_Gate or_1, 4 bits wide
  or or_2 (out_2, or_1_out[0], or_1_out[1], or_1_out[2], or_1_out[3]);
endmodule

module RamCtrl (
  input  Exec,
  input  Fetch,
  input  Load,
  input  Store,
  output MemLoad,
  output MemStore
);

  wire and_1_out;

  and and_1 (and_1_out, Exec, Load);
  and and_2 (MemStore, Exec, Store);
  or or_1 (MemLoad, Fetch, and_1_out);
endmodule

module Registres (
  input  [2:0] SR1,
  input  [15:0] IN,
  input  [2:0] SR2,
  input  WriteReg,
  input  [2:0] DR_SR,
  output [15:0] R0,
  output [15:0] OUT_SR1,
  output [15:0] R1,
  output [15:0] R2,
  output [15:0] R3,
  output [15:0] OUT_SR2,
  output [15:0] R4,
  output [15:0] R5,
  output [15:0] OUT_SR,
  output [15:0] R6,
  output [15:0] R7
);

  wire decoder_1_out0, decoder_1_out1, decoder_1_out2, decoder_1_out3, decoder_1_out4, decoder_1_out5,
       decoder_1_out6, decoder_1_out7;

  Decoder #(.select(3), .disabled(0)) decoder_1 (
    .out0(decoder_1_out0), .out1(decoder_1_out1), .out2(decoder_1_out2), .out3(decoder_1_out3),
    .out4(decoder_1_out4), .out5(decoder_1_out5), .out6(decoder_1_out6), .out7(decoder_1_out7), .sel(DR_SR),
    .en(WriteReg));
  Register #(.width(16), .trigger("falling")) u_R0 (.D(IN), .Q(R0), .clk(decoder_1_out0));  // open: en, clr
  Register #(.width(16), .trigger("falling")) u_R1 (.D(IN), .Q(R1), .clk(decoder_1_out1));  // open: en, clr
  Register #(.width(16), .trigger("falling")) u_R2 (.D(IN), .Q(R2), .clk(decoder_1_out2));  // open: en, clr
  Register #(.width(16), .trigger("falling")) u_R3 (.D(IN), .Q(R3), .clk(decoder_1_out3));  // open: en, clr
  Register #(.width(16), .trigger("falling")) u_R4 (.D(IN), .Q(R4), .clk(decoder_1_out4));  // open: en, clr
  Register #(.width(16), .trigger("falling")) u_R5 (.D(IN), .Q(R5), .clk(decoder_1_out5));  // open: en, clr
  Register #(.width(16), .trigger("falling")) u_R6 (.D(IN), .Q(R6), .clk(decoder_1_out6));  // open: en, clr
  Register #(.width(16), .trigger("falling")) u_R7 (.D(IN), .Q(R7), .clk(decoder_1_out7));  // open: en, clr
  Multiplexer #(.select(3), .width(16), .enable("false")) multiplexer_1 (
    .in0(R0), .in1(R1), .in2(R2), .in3(R3), .in4(R4), .in5(R5), .in6(R6), .in7(R7), .out(OUT_SR1), .sel(SR1));
  Multiplexer #(.select(3), .width(16), .enable("false")) multiplexer_2 (
    .in0(R0), .in1(R1), .in2(R2), .in3(R3), .in4(R4), .in5(R5), .in6(R6), .in7(R7), .out(OUT_SR2), .sel(SR2));
  Multiplexer #(.select(3), .width(16), .enable("false")) multiplexer_3 (
    .in0(R0), .in1(R1), .in2(R2), .in3(R3), .in4(R4), .in5(R5), .in6(R6), .in7(R7), .out(OUT_SR), .sel(DR_SR));
endmodule

module RegPC (
  input  H,
  input  Reset,
  input  [15:0] IR,
  input  [15:0] R,
  input  TestNZP,
  input  Jump,
  output [15:0] PC
);

  wire [3:0] LEA_out, ST_out, STR_out;
  wire [15:0] adder_1_out, adder_2_out, bit_extender_1_out, bit_extender_2_out, undriven;

  Adder #(.width(16)) adder_1 (.a(PC), .b({16{1'b0}}), .out(adder_1_out), .cin(1'b1));  // open: cout
  Register #(.width(16), .trigger("falling")) u_PC (.D(adder_1_out), .Q(PC), .clk(H), .clr(Reset));  // open: en
  assign bit_extender_1_out = {{7{IR[8]}}, IR[8:0]};  // Bit_Extender bit_extender_1
  assign bit_extender_2_out = {{10{IR[5]}}, IR[5:0]};  // Bit_Extender bit_extender_2
  // AND_Gate and_1 has open pins: in0=4'b0000, in1=IR[15:12], out=open
  Adder #(.width(16)) adder_2 (.a(undriven), .b(bit_extender_1_out), .out(adder_2_out));  // open: cin, cout
  assign LEA_out = IR[15:12] & 4'b1101;  // AND_Gate LEA, 4 bits wide
  assign ST_out = IR[15:12] & 4'b0011;  // AND_Gate ST, 4 bits wide
  assign STR_out = IR[15:12] & 4'b0111;  // AND_Gate STR, 4 bits wide

  // Notes on the sheet:
  //   Entrées non utilisées pour l'instant:
  //   PC <- PC + 1
  //   offset9
  //   offset6
endmodule

module CheckBR (
  input  [3:0] op_code,
  output yes_no
);

  wire or_1_out;

  or or_1 (or_1_out, op_code[0], op_code[1], op_code[2], op_code[3]);
  not not_1 (yes_no, or_1_out);

  // Notes on the sheet:
  //   si l'un des 4 bits vaut 1, ce n'est pas un BR
endmodule

module CheckJMP (
  input  [3:0] op_code,
  output yes_no
);

  wire and_1_out, nor_2_out, not_1_out, not_2_out, not_3_out, not_4_out, not_5_out, not_6_out, not_7_out,
       not_8_out, not_9_out, or_1_out;

  not not_1 (not_1_out, op_code[2]);
  not not_2 (not_2_out, op_code[3]);
  not not_3 (not_3_out, op_code[2]);
  not not_4 (not_4_out, op_code[3]);
  not not_5 (not_5_out, op_code[2]);
  not not_6 (not_6_out, op_code[3]);
  not not_7 (not_7_out, op_code[0]);
  not not_8 (not_8_out, op_code[1]);
  nor nor_1 (yes_no, op_code[0], op_code[1], not_1_out, not_2_out);
  nor nor_2 (nor_2_out, op_code[0], op_code[1], not_3_out, not_4_out);
  or or_1 (or_1_out, op_code[0], op_code[1], not_5_out, not_6_out);
  and and_1 (and_1_out, not_7_out, not_8_out, op_code[2], op_code[3]);
  LED led_1 (.in(nor_2_out));
  LED led_2 (.in(not_9_out));
  not not_9 (not_9_out, or_1_out);
  LED led_3 (.in(and_1_out));

  // Notes on the sheet:
  //   Basé sur le CheckBR, on peut vérifier facilement qu'un op-code correspond à ce qu'on veut :
  //   Si 1 de ses bits diffère de ce qu'on attend, ce n'est pas bon.
endmodule
